// Logisim project sd_final.circ as structural Verilog: 4 circuits, main circuit cronometro
module cronometro (
  input  \Válido ,
  output a,
  output b,
  output c,
  output d,
  output e,
  output f,
  output g
);

  wire and_1_out, and_2_out, and_3_out, and_4_out, and_5_out, and_6_out, and_7_out, and_8_out, and_9_out,
       and_10_out, and_11_out, and_12_out, and_13_out, and_14_out, and_15_out, and_16_out, and_17_out,
       clock_1_out, or_1_out, x0_q, x0_qn, x1_q, x1_qn, x2_q, x2_qn;

  and and_1 (and_1_out, x0_q, x1_q);
  or or_1 (or_1_out, \Válido , x0_q, x1_q, x2_q);
  Clock clock_1 (.out(clock_1_out));
  T_Flip_Flop x2 (.clk(clock_1_out), .T(and_1_out), .Q(x2_q), .Qn(x2_qn));  // open: preset, reset, en
  T_Flip_Flop x1 (.clk(clock_1_out), .T(x0_q), .Q(x1_q), .Qn(x1_qn));  // open: preset, reset, en
  T_Flip_Flop x0 (.clk(clock_1_out), .T(or_1_out), .Q(x0_q), .Qn(x0_qn));  // open: preset, reset, en
  and and_2 (and_2_out, x2_q, x0_q);
  and and_3 (and_3_out, x2_qn, x0_qn);
  and and_4 (and_4_out, x1_qn, x0_qn);
  and and_5 (and_5_out, x1_q, x0_q);
  and and_6 (and_6_out, x2_q, x1_qn);
  and and_7 (and_7_out, x2_q, x0_q);
  and and_8 (and_8_out, x1_qn, x0_q);
  and and_9 (and_9_out, x2_qn, x1_q, x0_qn);
  and and_10 (and_10_out, x0_q, x1_q);
  and and_11 (and_11_out, x1_q, x2_qn);
  and and_12 (and_12_out, x0_q, x2_qn);
  and and_13 (and_13_out, x0_q, x1_qn);
  and and_14 (and_14_out, x2_qn, x1_q);
  and and_15 (and_15_out, x2_q, x1_qn);
  or or_2 (a, and_2_out, x1_qn, and_3_out);
  or or_3 (b, and_4_out, x2_q, and_5_out);
  or or_4 (c, x0_qn, x2_qn, x1_q);
  or or_5 (d, and_6_out, and_7_out, and_8_out, and_9_out);
  and and_16 (and_16_out, x2_q, x0_q);
  or or_6 (e, and_16_out, and_17_out);
  and and_17 (and_17_out, x1_qn, x0_q);
  or or_7 (f, and_10_out, and_11_out, and_12_out);
  or or_8 (g, and_13_out, and_14_out, and_15_out);
endmodule

module semaforo_peoes (
  input  B_SV,
  output G,
  output Y,
  output R
);

  wire and_1_out, and_2_out, and_3_out, and_4_out, and_5_out, and_6_out, and_7_out, and_8_out, and_9_out,
       and_10_out, and_11_out, and_12_out, and_13_out, and_14_out, and_15_out, and_16_out, and_17_out,
       and_18_out, and_19_out, and_20_out, and_21_out, and_22_out, and_23_out, and_24_out, and_25_out,
       and_26_out, and_27_out, and_28_out, and_29_out, and_30_out, and_31_out, and_32_out, and_33_out,
       and_34_out, and_35_out, and_36_out, and_37_out, and_38_out, and_39_out, and_40_out, and_41_out,
       and_42_out, and_43_out, clock_1_out, not_1_out, or_1_out, or_2_out, or_3_out, or_4_out, or_5_out,
       or_6_out, or_7_out, or_8_out, or_9_out, or_10_out, or_11_out, or_12_out, or_13_out, or_14_out,
       or_15_out, or_16_out, or_17_out, x0_q, x0_qn, x1_q, x1_qn, x2_q, x2_qn, x3_q, x3_qn;

  not not_1 (not_1_out, B_SV);
  and and_1 (and_1_out, x2_q, x3_q, x0_q);
  and and_2 (and_2_out, x0_q, x1_q, x2_q);
  and and_3 (and_3_out, x2_q, x3_q, x0_q);
  and and_4 (and_4_out, x0_q, x1_q, x2_q);
  and and_5 (and_5_out, x0_q, x1_q);
  and and_6 (and_6_out, x0_q, x3_q, x2_q);
  and and_7 (and_7_out, x2_q, x3_q, x0_q);
  and and_8 (and_8_out, x1_q, x0_q);
  and and_9 (and_9_out, x0_q, x3_qn);
  and and_10 (and_10_out, x0_q, x2_qn);
  and and_11 (and_11_out, x2_qn, x0_q);
  and and_12 (and_12_out, x3_qn, x0_q);
  or or_1 (or_1_out, and_1_out, and_2_out);
  or or_2 (or_2_out, and_3_out, and_4_out);
  or or_3 (or_3_out, and_5_out, and_6_out);
  or or_4 (or_4_out, and_7_out, and_8_out);
  or or_5 (or_5_out, and_9_out, and_10_out);
  or or_6 (or_6_out, and_11_out, and_12_out);
  or or_7 (or_7_out, x2_q, x3_q, x1_q, x0_q);
  Clock clock_1 (.out(clock_1_out));
  and and_13 (and_13_out, or_1_out, not_1_out);
  or or_8 (or_8_out, and_13_out, and_14_out);
  and and_14 (and_14_out, B_SV, or_2_out);
  and and_15 (and_15_out, or_3_out, not_1_out);
  or or_9 (or_9_out, and_15_out, and_16_out);
  and and_16 (and_16_out, B_SV, or_4_out);
  and and_17 (and_17_out, or_5_out, not_1_out);
  or or_10 (or_10_out, and_17_out, and_18_out);
  and and_18 (and_18_out, B_SV, or_6_out);
  and and_19 (and_19_out, or_7_out, not_1_out);
  or or_11 (or_11_out, and_19_out, B_SV);
  T_Flip_Flop x3 (.clk(clock_1_out), .T(or_8_out), .Q(x3_q), .Qn(x3_qn));  // open: preset, reset, en
  T_Flip_Flop x2 (.clk(clock_1_out), .T(or_9_out), .Q(x2_q), .Qn(x2_qn));  // open: preset, reset, en
  T_Flip_Flop x1 (.clk(clock_1_out), .T(or_10_out), .Q(x1_q), .Qn(x1_qn));  // open: preset, reset, en
  T_Flip_Flop x0 (.clk(clock_1_out), .T(or_11_out), .Q(x0_q), .Qn(x0_qn));  // open: preset, reset, en
  and and_20 (and_20_out, x2_q, x3_qn);
  and and_21 (and_21_out, x1_q, x0_q, x3_qn);
  and and_22 (and_22_out, x3_q, x2_qn, x1_qn);
  and and_23 (and_23_out, x3_q, x1_q, x0_qn);
  and and_24 (and_24_out, x0_q, x1_q, x3_qn);
  and and_25 (and_25_out, x1_qn, x2_qn, x3_q);
  and and_26 (and_26_out, x0_qn, x1_q, x3_q);
  and and_27 (and_27_out, x2_q, x3_qn);
  and and_28 (and_28_out, x3_q, x2_q, x0_qn);
  and and_29 (and_29_out, x3_q, x1_q, x0_q);
  and and_30 (and_30_out, x0_q, x1_q, x3_q);
  and and_31 (and_31_out, x2_q, x0_qn, x3_q);
  and and_32 (and_32_out, x3_qn, x2_qn, x1_qn);
  and and_33 (and_33_out, x3_qn, x2_qn, x0_qn);
  and and_34 (and_34_out, x3_q, x2_q, x0_q);
  and and_35 (and_35_out, x0_q, x2_q, x3_q);
  and and_36 (and_36_out, x0_qn, x2_qn, x3_qn);
  and and_37 (and_37_out, x1_qn, x2_qn, x3_qn);
  or or_12 (or_12_out, and_20_out, and_21_out, and_22_out, and_23_out);
  or or_13 (or_13_out, and_24_out, and_25_out, and_26_out, and_27_out);
  or or_14 (or_14_out, and_28_out, and_29_out);
  or or_15 (or_15_out, and_30_out, and_31_out);
  or or_16 (or_16_out, and_32_out, and_33_out, and_34_out);
  or or_17 (or_17_out, and_35_out, and_36_out, and_37_out);
  and and_38 (and_38_out, or_12_out, not_1_out);
  or or_18 (G, and_38_out, and_39_out);
  and and_39 (and_39_out, B_SV, or_13_out);
  and and_40 (and_40_out, or_14_out, not_1_out);
  and and_41 (and_41_out, B_SV, or_15_out);
  and and_42 (and_42_out, or_16_out, not_1_out);
  and and_43 (and_43_out, B_SV, or_17_out);
  or or_19 (Y, and_40_out, and_41_out);
  or or_20 (R, and_42_out, and_43_out);
endmodule

module semaforo_carros (
  input  B_SV,
  input  P,
  output G,
  output Y,
  output R
);

  wire and_1_out, and_2_out, and_3_out, and_4_out, and_5_out, and_6_out, and_7_out, and_9_out, and_10_out,
       clock_1_out, not_1_out, or_1_out, or_2_out, x0_q, x0_qn, x1_q, x1_qn;

  not not_1 (not_1_out, P);
  and and_1 (and_1_out, B_SV, not_1_out);
  and and_2 (and_2_out, B_SV, x1_qn);
  and and_3 (and_3_out, x1_q, x0_qn);
  and and_4 (and_4_out, x0_q, x1_qn);
  and and_5 (and_5_out, not_1_out, x0_q);
  Clock clock_1 (.out(clock_1_out));
  and and_6 (and_6_out, not_1_out, x0_q);
  or or_1 (or_1_out, and_6_out, and_7_out);
  and and_7 (and_7_out, x0_q, x1_qn);
  T_Flip_Flop x1 (.clk(clock_1_out), .T(or_1_out), .Q(x1_q), .Qn(x1_qn));  // open: preset, reset, en
  T_Flip_Flop x0 (.clk(clock_1_out), .T(or_2_out), .Q(x0_q), .Qn(x0_qn));  // open: preset, reset, en
  or or_2 (or_2_out, and_1_out, and_2_out, and_3_out, and_5_out, and_4_out);
  and and_8 (G, x1_qn, x0_qn);
  and and_9 (and_9_out, x1_qn, x0_q);
  or or_3 (Y, and_9_out, and_10_out);
  and and_10 (and_10_out, x1_q, x0_qn);
  and and_11 (R, x0_q, x1_q);
endmodule

module circuito (
  input  B_SV
);

  wire Cronometro_a, Cronometro_b, Cronometro_c, Cronometro_d, Cronometro_e, Cronometro_f, Cronometro_g,
       or_1_out, S_Carros_g, S_Carros_r, S_Carros_y, S_Peoes_g, S_Peoes_r, S_Peoes_y;

  or or_1 (or_1_out, S_Peoes_y, S_Peoes_g);
  semaforo_peoes S_Peoes (.B_SV(B_SV), .G(S_Peoes_g), .Y(S_Peoes_y), .R(S_Peoes_r));
  semaforo_carros S_Carros (.B_SV(B_SV), .P(or_1_out), .G(S_Carros_g), .Y(S_Carros_y), .R(S_Carros_r));
  LED led_1 (.in(S_Peoes_r));
  LED led_2 (.in(S_Peoes_y));
  LED led_3 (.in(S_Peoes_g));
  LED led_4 (.in(S_Carros_r));
  LED led_5 (.in(S_Carros_y));
  LED led_6 (.in(S_Carros_g));
  cronometro Cronometro (
    .\Válido (S_Peoes_g), .a(Cronometro_a), .b(Cronometro_b), .c(Cronometro_c), .d(Cronometro_d),
    .e(Cronometro_e), .f(Cronometro_f), .g(Cronometro_g));
  _7_Segment_Display u_7_segment_display_1 (
    .g(Cronometro_g), .f(Cronometro_f), .a(Cronometro_a), .b(Cronometro_b), .e(Cronometro_e),
    .d(Cronometro_d), .c(Cronometro_c));  // open: dp
endmodule
