// Logisim project Logisim.circ as structural Verilog: 4 circuits, main circuit MC AGUA
module MC_AGUA (
  input  CM,
  input  SNA,
  input  STA,
  output VA,
  output RAQ,
  output CA
);

  wire and_1_out, clock_1_out, not_1_out, not_2_out, not_3_out, not_4_out, or_1_out, or_2_out, sna_x0_out,
       snax0_out, sta_x1_out, T0_q, T1_q, x1x0_2_out, x1x0_out;

  Clock clock_1 (.out(clock_1_out));
  not not_1 (not_1_out, T1_q);
  and x1x0 (x1x0_out, T1_q, T0_q);
  and snax0 (snax0_out, SNA, T0_q);
  and sta_x1 (sta_x1_out, STA, T1_q);
  and x1x0_2 (x1x0_2_out, T1_q, T0_q);
  and sna_x0 (sna_x0_out, SNA, T0_q);
  and and_1 (and_1_out, CM, not_1_out, not_2_out);
  not not_2 (not_2_out, T0_q);
  or or_1 (or_1_out, x1x0_out, snax0_out);
  T_Flip_Flop T1 (.clk(clock_1_out), .T(or_1_out), .Q(T1_q));  // open: Qn, preset, reset, en
  T_Flip_Flop T0 (.clk(clock_1_out), .T(or_2_out), .Q(T0_q));  // open: Qn, preset, reset, en
  or or_2 (or_2_out, sta_x1_out, x1x0_2_out, sna_x0_out, and_1_out);
  not not_3 (not_3_out, T1_q);
  not not_4 (not_4_out, T0_q);
  and and_2 (VA, not_3_out, T0_q);
  and x1_nx0 (RAQ, T1_q, not_4_out);
  and x1_x0 (CA, T1_q, T0_q);
endmodule

module MC_MAQUINA (
  input  BI,
  input  CA,
  input  CL,
  output CM
);

  wire and_1_out, and_2_out, and_3_out, and_4_out, clock_1_out, not_1_out, not_2_out, not_3_out, or_1_out,
       or_2_out, t_ff_1_q, t_ff_2_q;

  not not_1 (not_1_out, t_ff_1_q);
  not not_2 (not_2_out, t_ff_2_q);
  Clock clock_1 (.out(clock_1_out));
  and and_1 (and_1_out, CA, not_1_out, t_ff_2_q);
  and and_2 (and_2_out, CL, t_ff_1_q, not_2_out);
  and and_3 (and_3_out, BI, not_1_out, not_2_out);
  and and_4 (and_4_out, CA, not_1_out, t_ff_2_q);
  or or_1 (or_1_out, and_1_out, and_2_out);
  or or_2 (or_2_out, and_3_out, and_4_out);
  T_Flip_Flop t_ff_1 (.clk(clock_1_out), .T(or_1_out), .Q(t_ff_1_q));  // open: Qn, preset, reset, en
  T_Flip_Flop t_ff_2 (.clk(clock_1_out), .T(or_2_out), .Q(t_ff_2_q));  // open: Qn, preset, reset, en
  not not_3 (not_3_out, t_ff_1_q);
  and and_5 (CM, not_3_out, t_ff_2_q);
endmodule

module MAIN (
  input  BI,
  input  SNA,
  input  STA,
  output VA,
  output RAQ,
  output MD,
  output ME,
  output BA,
  output BA___MC
);

  wire mc_agua_1_ca, mc_lavagem_1_cl, mc_maquina_1_cm;

  MC_MAQUINA mc_maquina_1 (.BI(BI), .CA(mc_agua_1_ca), .CL(mc_lavagem_1_cl), .CM(mc_maquina_1_cm));
  MC_AGUA mc_agua_1 (.CM(mc_maquina_1_cm), .SNA(SNA), .STA(STA), .VA(VA), .RAQ(RAQ), .CA(mc_agua_1_ca));
  MC_LAVAGEM mc_lavagem_1 (
    .CA(mc_agua_1_ca), .SNA(SNA), .MD(MD), .ME(ME), .BA(BA), .BA___MC(BA___MC), .CL(mc_lavagem_1_cl));
endmodule

module MC_LAVAGEM (
  input  CA,
  input  SNA,
  output MD,
  output ME,
  output BA,
  output BA___MC,
  output CL
);

  wire and_1_out, and_2_out, and_3_out, and_4_out, clock_1_out, not_1_out, not_2_out, not_3_out, not_4_out,
       not_5_out, nsna_x0_out, nsna_x2_out, nx0_ca_out, nx2_ca_out, nx2_x0_nca_out, nx2_x0_out, or_1_out,
       or_2_out, T0_q, T1_q, T2_q, x1_x0_out, x2_nx0_nca_out;

  not not_1 (not_1_out, CA);
  not not_2 (not_2_out, SNA);
  not not_3 (not_3_out, T2_q);
  not not_4 (not_4_out, T1_q);
  not not_5 (not_5_out, T0_q);
  Clock clock_1 (.out(clock_1_out));
  and x1_x0 (x1_x0_out, T1_q, T0_q);
  and nsna_x0 (nsna_x0_out, T0_q, not_2_out);
  and nx2_x0 (nx2_x0_out, not_3_out, T0_q);
  and nx2_ca (nx2_ca_out, not_3_out, CA);
  and nx0_ca (nx0_ca_out, not_5_out, CA);
  and nsna_x2 (nsna_x2_out, not_2_out, T2_q);
  and x2_nx0_nca (x2_nx0_nca_out, T2_q, not_5_out, not_1_out);
  and nx2_x0_nca (nx2_x0_nca_out, not_3_out, T0_q, not_1_out);
  T_Flip_Flop T2 (.clk(clock_1_out), .T(x1_x0_out), .Q(T2_q));  // open: Qn, preset, reset, en
  or or_1 (or_1_out, x1_x0_out, nsna_x0_out, nx2_x0_out);
  or or_2 (or_2_out, T1_q, nx2_ca_out, nx0_ca_out, nsna_x2_out, x2_nx0_nca_out, nx2_x0_nca_out);
  and and_1 (and_1_out, not_3_out, not_4_out, T0_q);
  or or_3 (MD, and_1_out, and_2_out);
  and and_2 (and_2_out, not_3_out, T1_q, not_5_out);
  and and_3 (and_3_out, T2_q, not_4_out, not_5_out);
  or or_4 (ME, and_3_out, and_4_out);
  and and_4 (and_4_out, not_3_out, T1_q, T0_q);
  and and_5 (BA, T2_q, not_4_out, T0_q);
  and and_6 (BA___MC, T2_q, T1_q, not_5_out);
  and and_7 (CL, T2_q, T1_q, T0_q);
  T_Flip_Flop T1 (.clk(clock_1_out), .T(or_1_out), .Q(T1_q));  // open: Qn, preset, reset, en
  T_Flip_Flop T0 (.clk(clock_1_out), .T(or_2_out), .Q(T0_q));  // open: Qn, preset, reset, en
endmodule
